# Fritzing sketch pcb-in-a-box (saved by Fritzing 0.7.12b)
breadboards: 1

parts:
  Arduino1 = Arduino
  R1 = Rotary Potentiometer (Large) [maximum_resistance=100kΩ package=THT]
  R2 = Rotary Potentiometer (Large) [maximum_resistance=100kΩ package=THT]
  R4 = Trimmer Potentiometer [maximum_resistance=10kΩ package=THT]
  LCD1 = LCD screen
  LED1 = Blue LED - 5mm
  LED2 = Blue LED - 5mm
  LED3 = Blue LED - 5mm
  LED4 = Blue LED - 5mm
  LED5 = Blue LED - 5mm
  LED6 = Blue LED - 5mm
  R5 = 10 Ω Resistor [package=THT]
  R6 = 10 Ω Resistor [package=THT]
  R7 = 10 Ω Resistor [package=THT]
  R8 = 10 Ω Resistor [package=THT]
  LED7 = green LED - 5mm
  LED8 = LED - 5mm [color="Red (633nm)" package="5 mm [THT]"]
  S1 = Pushbutton [package="[THT]"]
  S2 = Pushbutton [package="[THT]"]

nets:
  N1: Arduino1.GND, R5.Pin_0, R6.Pin_0
  N2: Arduino1.D13, S1.Pin_3, S1.Pin_4
  N3: Arduino1.D12, Arduino1.D11, R7.Pin_0, R8.Pin_0
  N4: Arduino1.D10, LED1.anode, LED2.anode, LED3.anode
  N5: Arduino1.D9, LED4.anode, LED5.anode, LED6.anode
  N6: Arduino1.D8, S2.Pin_3, S2.Pin_4
  N7: Arduino1.D7, LCD1.RS
  N8: Arduino1.D6, LCD1.E
  N9: Arduino1.D5, LCD1.DB4
  N10: Arduino1.D4, LCD1.DB5
  N11: Arduino1.D3, LCD1.DB6
  N12: Arduino1.D2, LCD1.DB7
  N13: Arduino1.A0, R1.wiper
  N14: Arduino1.A1, R2.wiper
  N15: R2.leg2, LCD1.VSS, LCD1.R/W, LCD1.LED-, LED7.cathode, LED8.cathode, S1.Pin_1, S1.Pin_2, S2.Pin_1, S2.Pin_2
  N16: R4.wiper, LCD1.V0
  N17: LCD1.VDD, LCD1.LED+
  N18: LED1.cathode, LED2.cathode, LED3.cathode, R6.Pin_1
  N19: LED4.cathode, LED5.cathode, LED6.cathode, R5.Pin_1
  N20: R7.Pin_1, LED8.anode
  N21: R8.Pin_1, LED7.anode

notes:
  Nesta Versão ainda falta calcular os valores dos compoentes.
  Porque Potenciometros?
  Os Potenciomentros é uma segunda proposta substituindo os botões que selecionam a intencidade da luz e o tempo.
  LCD
  Usado um LCD Comum
  Não temos ainda um LCD i2C
